# Fritzing sketch Auto Plant Watering (saved by Fritzing 0.9.3b)
breadboards: 1

parts:
  Part1 = Arduino Uno (Rev3)
  Part2 = Soil Moisture Sensor
  WeMos_D1_Mini_Relay_Shield_V1 = WeMos D1 Mini Relay Shield V2
  HLK-PM1 = HLK-PM12 [part_number=HLK-PM12]
  LED1 = LED - 3mm [color="Red (633nm)" package="3 mm [THT]"]

nets:
  N1: Part1.A0, Part2.SIG
  N2: Part1.D8, WeMos_D1_Mini_Relay_Shield_V1.D1
  5V: Part1.5V, Part2.VCC, WeMos_D1_Mini_Relay_Shield_V1.5V
  GND: Part1.GND, Part2.GND, WeMos_D1_Mini_Relay_Shield_V1.G
  N3: WeMos_D1_Mini_Relay_Shield_V1.COM, LED1.cathode
  N4: WeMos_D1_Mini_Relay_Shield_V1.NO, HLK-PM1.+Vo
  N5: HLK-PM1.-Vo, LED1.anode

// code stored in the sketch: WaterGardening.ino


#define RELAY1  8                        



void setup() {
  // put your setup code here, to run once:
  Serial.begin(9600);
  pinMode(RELAY1, OUTPUT);    
  // initialize digital pin LED_BUILTIN as an output.
  pinMode(LED_BUILTIN, OUTPUT);   

}

void loop() {
    // put your main code here, to run repeatedly:
  int moistureSensor=analogRead(A0); // Incoming analog signal read and appointed sensor
  if (moistureSensor>600){
        // turn on relay
    digitalWrite(RELAY1,LOW); 
    digitalWrite(LED_BUILTIN, HIGH);      
    Serial.println("Relay ON");       

  }else{
    //turn off relay
    digitalWrite(RELAY1,HIGH);          
    digitalWrite(LED_BUILTIN, LOW);    
    Serial.println("Relay OFF");

  }
  delay(5000);                                      
}
